// Logisim project Circuitos-M2.circ as structural Verilog: 5 circuits, main circuit main
module main (
  input  [7:0] in_1,
  input  in_2,
  output [7:0] out_3
);

  wire button_1_out, clock_1_out;

  Clock clock_1 (.out(clock_1_out));
  Button button_1 (.out(button_1_out));
  Register register_1 (.D(in_1), .en(in_2), .Q(out_3), .clk(clock_1_out), .clr(button_1_out));
endmodule

module Encoder_8_bits (
  output out_1,
  output out_2,
  output out_3,
  output out_4
);

  wire L_out, N_out, Ne_out, No_out, O_out, S_out, Se_out, So_out;

  Button No (.out(No_out));
  Button O (.out(O_out));
  Button So (.out(So_out));
  Button N (.out(N_out));
  Button Ne (.out(Ne_out));
  Button L (.out(L_out));
  Button Se (.out(Se_out));
  Button S (.out(S_out));
  or or_1 (out_2, No_out, O_out, So_out, S_out);
  or or_2 (out_3, No_out, O_out, Se_out, L_out);
  ExactlyOne xor_1 (
    .out(out_1), .in0(N_out), .in1(Ne_out), .in2(L_out), .in3(Se_out), .in4(S_out), .in5(So_out),
    .in6(O_out), .in7(No_out));
  or or_3 (out_4, No_out, So_out, Se_out, Ne_out);
endmodule

module Multiplexer (
  input  [15:0] in_1,
  input  [15:0] in_2,
  input  [15:0] in_3,
  input  [15:0] in_4,
  input  [15:0] in_5,
  input  [15:0] in_6,
  input  [15:0] in_7,
  input  [15:0] in_8,
  input  [2:0] in_9,
  output [18:0] out_10
);

  wire and_1_out, and_2_out, and_3_out, and_4_out, and_5_out, and_6_out, and_7_out, and_8_out, not_1_out,
       not_2_out, not_3_out, not_4_out, not_5_out, not_6_out, not_7_out, not_8_out, not_9_out, not_10_out,
       not_11_out, not_12_out;

  not not_1 (not_1_out, in_9[2]);
  assign out_10[15:0] = and_1_out ? in_1 : 16'bz;  // Controlled_Buffer controlled_buffer_1
  assign out_10[15:0] = and_2_out ? in_2 : 16'bz;  // Controlled_Buffer controlled_buffer_2
  and and_1 (and_1_out, not_1_out, not_5_out, not_3_out);
  and and_2 (and_2_out, not_2_out, not_4_out, in_9[0]);
  not not_2 (not_2_out, in_9[2]);
  not not_3 (not_3_out, in_9[0]);
  not not_4 (not_4_out, in_9[1]);
  not not_5 (not_5_out, in_9[1]);
  not not_6 (not_6_out, in_9[2]);
  assign out_10[15:0] = and_3_out ? in_3 : 16'bz;  // Controlled_Buffer controlled_buffer_3
  assign out_10[15:0] = and_4_out ? in_4 : 16'bz;  // Controlled_Buffer controlled_buffer_4
  and and_3 (and_3_out, not_6_out, in_9[1], not_8_out);
  and and_4 (and_4_out, not_7_out, in_9[1], in_9[0]);
  not not_7 (not_7_out, in_9[2]);
  not not_8 (not_8_out, in_9[0]);
  assign out_10[15:0] = and_6_out ? in_5 : 16'bz;  // Controlled_Buffer controlled_buffer_5
  assign out_10[15:0] = and_5_out ? in_6 : 16'bz;  // Controlled_Buffer controlled_buffer_6
  and and_5 (and_5_out, in_9[2], not_11_out, in_9[0]);
  and and_6 (and_6_out, in_9[2], not_9_out, not_10_out);
  not not_9 (not_9_out, in_9[1]);
  not not_10 (not_10_out, in_9[0]);
  not not_11 (not_11_out, in_9[1]);
  assign out_10[15:0] = and_8_out ? in_7 : 16'bz;  // Controlled_Buffer controlled_buffer_7
  assign out_10[15:0] = and_7_out ? in_8 : 16'bz;  // Controlled_Buffer controlled_buffer_8
  and and_7 (and_7_out, in_9[2], in_9[1], in_9[0]);
  and and_8 (and_8_out, in_9[2], in_9[1], not_12_out);
  not not_12 (not_12_out, in_9[0]);

  assign out_10[18:16] = in_9;
endmodule

module Demux (
  input  [18:0] in_1
);

  wire not_1_out, not_2_out, not_3_out, not_4_out, not_5_out, not_6_out, not_7_out, not_8_out, not_9_out,
       not_10_out, not_11_out, not_12_out;

  // AND_Gate and_1 has open pins: in0=not_1_out, in1=not_2_out, in2=not_5_out, out=open
  not not_1 (not_1_out, in_1[18]);
  not not_2 (not_2_out, in_1[17]);
  // AND_Gate and_2 has open pins: in0=not_4_out, in1=not_6_out, in2=in_1[16], out=open
  // AND_Gate and_3 has open pins: in0=not_3_out, in1=in_1[17], in2=not_7_out, out=open
  not not_3 (not_3_out, in_1[18]);
  not not_4 (not_4_out, in_1[18]);
  not not_5 (not_5_out, in_1[16]);
  not not_6 (not_6_out, in_1[17]);
  // AND_Gate and_4 has open pins: in0=not_8_out, in1=in_1[17], in2=in_1[16], out=open
  // AND_Gate and_5 has open pins: in0=in_1[18], in1=not_9_out, in2=not_10_out, out=open
  not not_7 (not_7_out, in_1[16]);
  not not_8 (not_8_out, in_1[18]);
  not not_9 (not_9_out, in_1[17]);
  // AND_Gate and_6 has open pins: in0=in_1[18], in1=not_11_out, in2=in_1[16], out=open
  // AND_Gate and_7 has open pins: in0=in_1[18], in1=in_1[17], in2=not_12_out, out=open
  not not_10 (not_10_out, in_1[16]);
  not not_11 (not_11_out, in_1[17]);
  // AND_Gate and_8 has open pins: in0=in_1[18], in1=in_1[17], in2=in_1[16], out=open
  not not_12 (not_12_out, in_1[16]);
endmodule

module multiplexer_do_logsim (
  input  [15:0] in_1,
  input  [15:0] in_2,
  input  [15:0] in_3,
  input  [15:0] in_4,
  input  [15:0] in_5,
  input  [15:0] in_6,
  input  [15:0] in_7,
  input  [15:0] in_8,
  input  in_9,
  output [15:0] out_10,
  output [15:0] out_11,
  output [15:0] out_12,
  output [15:0] out_13,
  output [15:0] out_14,
  output [15:0] out_15,
  output [15:0] out_16,
  output [15:0] out_17
);

  wire button_1_out, button_2_out, clock_1_out, comparator_1_eq, counter_1_carry, demultiplexer_2_out0,
       demultiplexer_2_out1, demultiplexer_2_out2, demultiplexer_2_out3, demultiplexer_2_out4,
       demultiplexer_2_out5, demultiplexer_2_out6, demultiplexer_2_out7, or_1_out;
  wire [2:0] counter_1_q;
  wire [7:0] counter_2_q;
  wire [15:0] demultiplexer_1_out0, demultiplexer_1_out1, demultiplexer_1_out2, demultiplexer_1_out3,
       demultiplexer_1_out4, demultiplexer_1_out5, demultiplexer_1_out6, demultiplexer_1_out7;
  wire [18:0] multiplexer_1_out_10;

  Clock clock_1 (.out(clock_1_out));
  Multiplexer multiplexer_1 (
    .in_1(in_1), .in_2(in_2), .in_3(in_3), .in_4(in_4), .in_5(in_5), .in_6(in_6), .in_7(in_7), .in_8(in_8),
    .in_9(counter_1_q), .out_10(multiplexer_1_out_10));
  Counter #(.width(3), .max('h7)) counter_1 (
    .Q(counter_1_q), .carry(counter_1_carry), .clk(clock_1_out), .clr(or_1_out));  // open: load, D, count
  Counter #(.max('h7), .ongoal("stay")) counter_2 (
    .Q(counter_2_q), .clk(counter_1_carry), .clr(button_1_out));  // open: load, D, count, carry
  Demultiplexer #(.select(3), .width(16)) demultiplexer_1 (
    .out0(demultiplexer_1_out0), .out1(demultiplexer_1_out1), .out2(demultiplexer_1_out2),
    .out3(demultiplexer_1_out3), .out4(demultiplexer_1_out4), .out5(demultiplexer_1_out5),
    .out6(demultiplexer_1_out6), .out7(demultiplexer_1_out7), .in(multiplexer_1_out_10[15:0]),
    .sel(multiplexer_1_out_10[18:16]));  // open: en
  or or_1 (or_1_out, comparator_1_eq, button_1_out);
  Comparator comparator_1 (.a(counter_2_q), .b(8'h7), .eq(comparator_1_eq));  // open: gt, lt
  Button button_1 (.out(button_1_out));
  Demultiplexer #(.select(3)) demultiplexer_2 (
    .out0(demultiplexer_2_out0), .out1(demultiplexer_2_out1), .out2(demultiplexer_2_out2),
    .out3(demultiplexer_2_out3), .out4(demultiplexer_2_out4), .out5(demultiplexer_2_out5),
    .out6(demultiplexer_2_out6), .out7(demultiplexer_2_out7), .in(clock_1_out),
    .sel(multiplexer_1_out_10[18:16]));  // open: en
  Register #(.width(16)) register_1 (
    .D(demultiplexer_1_out0), .en(in_9), .Q(out_10), .clk(demultiplexer_2_out0), .clr(button_2_out));
  Register #(.width(16)) register_2 (
    .D(demultiplexer_1_out1), .en(in_9), .Q(out_11), .clk(demultiplexer_2_out1), .clr(button_2_out));
  Register #(.width(16)) register_3 (
    .D(demultiplexer_1_out2), .en(in_9), .Q(out_12), .clk(demultiplexer_2_out2), .clr(button_2_out));
  Register #(.width(16)) register_4 (
    .D(demultiplexer_1_out3), .en(in_9), .Q(out_13), .clk(demultiplexer_2_out3), .clr(button_2_out));
  Register #(.width(16)) register_5 (
    .D(demultiplexer_1_out4), .en(in_9), .Q(out_14), .clk(demultiplexer_2_out4), .clr(button_2_out));
  Register #(.width(16)) register_6 (
    .D(demultiplexer_1_out5), .en(in_9), .Q(out_15), .clk(demultiplexer_2_out5), .clr(button_2_out));
  Register #(.width(16)) register_7 (
    .D(demultiplexer_1_out6), .en(in_9), .Q(out_16), .clk(demultiplexer_2_out6), .clr(button_2_out));
  Register #(.width(16)) register_8 (
    .D(demultiplexer_1_out7), .en(in_9), .Q(out_17), .clk(demultiplexer_2_out7), .clr(button_2_out));
  Button button_2 (.out(button_2_out));
endmodule
